// Logisim project Relogio Digital.circ as structural Verilog
module Relogio (
);

  wire clock_1_out, clock_2_out, contador_0_59_1_prox_clk, contador_0_59_2_prox_clk, Reset_out;
  wire [3:0] contador_0_23_1_dezena, contador_0_23_1_unidade, contador_0_59_1_dezena,
       contador_0_59_1_unidade, contador_0_59_2_dezena, contador_0_59_2_unidade;

  Hex_Digit_Display hex_digit_display_1 (.value(contador_0_23_1_dezena));  // open: dp
  LED led_1 (.in(1'b1));
  LED led_2 (.in(1'b1));
  Hex_Digit_Display hex_digit_display_2 (.value(contador_0_23_1_unidade));  // open: dp
  Contador_0_23 contador_0_23_1 (
    .Dezena(contador_0_23_1_dezena), .CLK(contador_0_59_1_prox_clk), .Unidade(contador_0_23_1_unidade),
    .Reset(Reset_out));  // open: Prox_CLK
  Hex_Digit_Display hex_digit_display_3 (.value(contador_0_59_1_unidade));  // open: dp
  Hex_Digit_Display hex_digit_display_4 (.value(contador_0_59_1_dezena));  // open: dp
  Contador_0_59 contador_0_59_1 (
    .Dezena(contador_0_59_1_dezena), .CLK(contador_0_59_2_prox_clk), .Unidade(contador_0_59_1_unidade),
    .Prox_CLK(contador_0_59_1_prox_clk), .Reset(Reset_out));
  Clock clock_1 (.out(clock_1_out));
  LED led_3 (.in(clock_1_out));
  LED led_4 (.in(clock_1_out));
  Hex_Digit_Display hex_digit_display_5 (.value(contador_0_59_2_dezena));  // open: dp
  Clock clock_2 (.out(clock_2_out));
  Hex_Digit_Display hex_digit_display_6 (.value(contador_0_59_2_unidade));  // open: dp
  Contador_0_59 contador_0_59_2 (
    .Dezena(contador_0_59_2_dezena), .CLK(clock_2_out), .Unidade(contador_0_59_2_unidade),
    .Prox_CLK(contador_0_59_2_prox_clk), .Reset(Reset_out));
  Button Reset (.out(Reset_out));
endmodule

module Contador_0_9 (
  input  CLK,
  input  Reset,
  output [3:0] \Saída ,
  output Prox_CLK
);

  wire or_1_out;
  wire [3:0] adder_1_out;

  Register #(.width(4)) register_1 (.D(adder_1_out), .Q(\Saída ), .clk(CLK), .clr(or_1_out));  // open: en
  or or_1 (or_1_out, Prox_CLK, Reset);
  Hex_Digit_Display hex_digit_display_1 (.value(\Saída ));  // open: dp
  Adder #(.width(4)) adder_1 (.a(\Saída ), .b(4'b0001), .out(adder_1_out));  // open: cin, cout
  and and_1 (Prox_CLK, \Saída [1], \Saída [3]);
endmodule

module Contador_0_59 (
  input  CLK,
  input  Reset,
  output [3:0] Dezena,
  output [3:0] Unidade,
  output Prox_CLK
);

  wire contador_0_9_2_prox_clk, or_1_out;

  or or_1 (or_1_out, Reset, Prox_CLK);
  Hex_Digit_Display hex_digit_display_1 (.value(Dezena));  // open: dp
  Contador_0_9 contador_0_9_1 (.CLK(contador_0_9_2_prox_clk), .Reset(or_1_out), .\Saída (Dezena));  // open: Prox_CLK
  Hex_Digit_Display hex_digit_display_2 (.value(Unidade));  // open: dp
  Contador_0_9 contador_0_9_2 (.CLK(CLK), .Reset(or_1_out), .\Saída (Unidade), .Prox_CLK(contador_0_9_2_prox_clk));
  nor nor_1 (Prox_CLK, Dezena[3], ~Dezena[2], ~Dezena[1], Dezena[0], Unidade[3], Unidade[2], Unidade[1], Unidade[0]);  // NOR_Gate
endmodule

module Contador_0_23 (
  input  CLK,
  input  Reset,
  output [3:0] Dezena,
  output [3:0] Unidade,
  output Prox_CLK
);

  wire contador_0_9_2_prox_clk, or_1_out;

  or or_1 (or_1_out, Reset, Prox_CLK);
  Hex_Digit_Display hex_digit_display_1 (.value(Dezena));  // open: dp
  Contador_0_9 contador_0_9_1 (.CLK(contador_0_9_2_prox_clk), .Reset(or_1_out), .\Saída (Dezena));  // open: Prox_CLK
  Hex_Digit_Display hex_digit_display_2 (.value(Unidade));  // open: dp
  Contador_0_9 contador_0_9_2 (.CLK(CLK), .Reset(or_1_out), .\Saída (Unidade), .Prox_CLK(contador_0_9_2_prox_clk));
  nor nor_1 (Prox_CLK, Dezena[3], Dezena[2], ~Dezena[1], Dezena[0], Unidade[3], ~Unidade[2], Unidade[1], Unidade[0]);  // NOR_Gate
endmodule
